// Logisim project ATM.circ as structural Verilog
module main (
  input  ret_alta_suma,
  input  DELETE_EXIT,
  input  ret10,
  input  OK,
  input  ret20,
  input  sw1,
  input  sw0,
  input  ret50,
  input  ret100,
  input  ret200,
  input  ret500,
  input  nr5,
  input  nr4,
  input  nr3,
  input  nr2,
  input  nr1,
  input  nr0,
  output ERROR,
  output Insert_PIN,
  output selectOP,
  output OP_FIN,
  output InsertSUM,
  output InsertBILLS,
  output interogare,
  output retragere,
  output depunere,
  output transfer,
  output calculating,
  output [6:0] ssd5,
  output [6:0] ssd4,
  output [6:0] ssd3,
  output [6:0] ssd2,
  output [6:0] ssd1,
  output [6:0] ssd0
);

  wire CLK_out, comparator_egalitate_v2_1_i, comparator_egalitate_v2_2_i, comparator_egalitate_v2_3_i,
       comparator_egalitate_v2_4_i, comparator_sold_suma_1_i, comparator_sold_suma_2_i, demux_2out1bit_1_y0,
       demux_2out1bit_1_y1, demux_4out1bit_1_y0, demux_4out1bit_1_y1, demux_4out1bit_1_y2,
       demux_4out1bit_1_y3, distribuitor_bani_1_done, distribuitor_bani_1_eroare,
       divizor_frecventa_1_clk_1hz, or_1_out, or_2_out, uc_1_clr_nr, uc_1_en_ad_sc, uc_1_en_distr,
       uc_1_en_nr2, uc_1_op_ad_sc, uc_1_sel_pin, uc_1_sel_w_in, uc_1_we2, uc_1_we16, uc_1_we_bank, undriven,
       undriven_2, undriven_3, undriven_4, undriven_5, undriven_6, undriven_7, undriven_8, undriven_9,
       undriven_10, undriven_11, undriven_12, undriven_13, undriven_14, undriven_15, undriven_16,
       undriven_17, undriven_18, undriven_19, undriven_20, undriven_21, undriven_22, undriven_23,
       undriven_24, undriven_25, undriven_26, undriven_27, undriven_28, undriven_29, undriven_30,
       undriven_31, undriven_32, undriven_33, undriven_34, undriven_35, undriven_36, undriven_37,
       undriven_38, undriven_39, undriven_40, undriven_41, undriven_42;
  wire [1:0] codificator_4in2out_1_iesire, demux_2out2bit_1_y0, demux_2out2bit_1_y1, mux_2in2bit_1_y,
       mux_2in2bit_2_y, mux_2in2bit_3_y, PIN_PRINCIPAL_iesire, PIN_TR_iesire, uc_1_sel_ssd, uc_1_sel_val16;
  wire [3:0] binary_to_bcd_1_bcd0, binary_to_bcd_1_bcd1, binary_to_bcd_1_bcd2, binary_to_bcd_1_bcd3,
       binary_to_bcd_1_bcd4, cash_register_1_cashreg10, cash_register_1_cashreg20, cash_register_1_cashreg50,
       cash_register_1_cashreg100, cash_register_1_cashreg200, cash_register_1_cashreg500,
       distribuitor_bani_1_bani10, distribuitor_bani_1_bani20, distribuitor_bani_1_bani50,
       distribuitor_bani_1_bani100, distribuitor_bani_1_bani200, distribuitor_bani_1_bani500,
       distribuitor_bani_1_rest10, distribuitor_bani_1_rest20, distribuitor_bani_1_rest50,
       distribuitor_bani_1_rest100, distribuitor_bani_1_rest200, distribuitor_bani_1_rest500, i0_count,
       i1_count, i2_count, i3_count, mux_for_cash_reg_1_reg10, mux_for_cash_reg_1_reg20,
       mux_for_cash_reg_1_reg50, mux_for_cash_reg_1_reg100, mux_for_cash_reg_1_reg200,
       mux_for_cash_reg_1_reg500, mux_in_or0_4bit_1_y, mux_in_or0_4bit_2_y, mux_ssd4_1_y, mux_ssd_1_y,
       mux_ssd_2_y, mux_ssd_3_y, mux_ssd_4_y, mux_ssd_5_y, numarator_0_9_1_count, numarator_0_9_2_count,
       registru_pin_0_1_i0, registru_pin_0_1_i1, registru_pin_0_1_i2, registru_pin_0_1_i3,
       registru_pin_1_1_i0, registru_pin_1_1_i1, registru_pin_1_1_i2, registru_pin_1_1_i3,
       registru_pin_2_1_i0, registru_pin_2_1_i1, registru_pin_2_1_i2, registru_pin_2_1_i3,
       registru_pin_3_1_i0, registru_pin_3_1_i1, registru_pin_3_1_i2, registru_pin_3_1_i3,
       sum_nr_bills_1_newreg10, sum_nr_bills_1_newreg20, sum_nr_bills_1_newreg50, sum_nr_bills_1_newreg100,
       sum_nr_bills_1_newreg200, sum_nr_bills_1_newreg500;
  wire [15:0] bcd_to_binary_1_bin, bcd_to_binary_2_bin, bills_to_sum_1_sum, cash_register_sold_1_sold,
       mux_3in16bit_1_y, mux_4in16bit_1_y, mux_4in16bit_2_y, optiuni_retragere_suma_1_suma,
       registru_16_incarcare0_1_iesire, registru_16_incarcare1_1_iesire, registru_16_incarcare2_1_iesire,
       registru_16_incarcare3_1_iesire, sumator_scazator_16b_1_c;

  demux_4out1bit demux_4out1bit_1 (
    .I(uc_1_we16), .S(mux_2in2bit_1_y), .Y0(demux_4out1bit_1_y0), .Y1(demux_4out1bit_1_y1),
    .Y2(demux_4out1bit_1_y2), .Y3(demux_4out1bit_1_y3));
  mux_2in2bit mux_2in2bit_1 (.I0(PIN_PRINCIPAL_iesire), .I1(PIN_TR_iesire), .S(uc_1_sel_pin), .Y(mux_2in2bit_1_y));
  numarator_0_9 numarator_0_9_1 (.ENABLE(nr5), .RESET(or_2_out), .CLK(CLK_out), .COUNT(numarator_0_9_1_count));
  numarator_0_9 numarator_0_9_2 (.ENABLE(nr4), .RESET(or_2_out), .CLK(CLK_out), .COUNT(numarator_0_9_2_count));
  numarator_0_9 i3 (.ENABLE(nr3), .RESET(or_2_out), .CLK(CLK_out), .COUNT(i3_count));
  numarator_0_9 i2 (.ENABLE(nr2), .RESET(or_2_out), .CLK(CLK_out), .COUNT(i2_count));
  numarator_0_9 i1 (.ENABLE(nr1), .RESET(or_2_out), .CLK(CLK_out), .COUNT(i1_count));
  numarator_0_9 i0 (.ENABLE(nr0), .RESET(or_2_out), .CLK(CLK_out), .COUNT(i0_count));
  divizor_frecventa divizor_frecventa_1 (.clk_100mhz(CLK_out), .reset(or_2_out), .clk_1hz(divizor_frecventa_1_clk_1hz));
  registru_PIN_3 registru_pin_3_1 (
    .clk(CLK_out), .I0(registru_pin_3_1_i0), .I1(registru_pin_3_1_i1), .I2(registru_pin_3_1_i2),
    .I3(registru_pin_3_1_i3));
  registru_PIN_2 registru_pin_2_1 (
    .clk(CLK_out), .I0(registru_pin_2_1_i0), .I1(registru_pin_2_1_i1), .I2(registru_pin_2_1_i2),
    .I3(registru_pin_2_1_i3));
  registru_PIN_1 registru_pin_1_1 (
    .clk(CLK_out), .I0(registru_pin_1_1_i0), .I1(registru_pin_1_1_i1), .I2(registru_pin_1_1_i2),
    .I3(registru_pin_1_1_i3));
  registru_PIN_0 registru_pin_0_1 (
    .clk(CLK_out), .I0(registru_pin_0_1_i0), .I1(registru_pin_0_1_i1), .I2(registru_pin_0_1_i2),
    .I3(registru_pin_0_1_i3));
  registru_16_incarcare3 registru_16_incarcare3_1 (
    .clk(CLK_out), .we(demux_4out1bit_1_y3), .incarcare(sumator_scazator_16b_1_c),
    .iesire(registru_16_incarcare3_1_iesire));
  registru_16_incarcare2 registru_16_incarcare2_1 (
    .clk(CLK_out), .we(demux_4out1bit_1_y2), .incarcare(sumator_scazator_16b_1_c),
    .iesire(registru_16_incarcare2_1_iesire));
  registru_16_incarcare1 registru_16_incarcare1_1 (
    .clk(CLK_out), .we(demux_4out1bit_1_y1), .incarcare(sumator_scazator_16b_1_c),
    .iesire(registru_16_incarcare1_1_iesire));
  registru_16_incarcare0 registru_16_incarcare0_1 (
    .clk(CLK_out), .we(demux_4out1bit_1_y0), .incarcare(sumator_scazator_16b_1_c),
    .iesire(registru_16_incarcare0_1_iesire));
  bcd_to_binary bcd_to_binary_1 (.i0(i0_count), .i1(i1_count), .i2(i2_count), .i3(i3_count), .bin(bcd_to_binary_1_bin));
  bills_to_sum bills_to_sum_1 (
    .bani10(numarator_0_9_1_count), .bani20(numarator_0_9_2_count), .bani50(i3_count), .bani100(i2_count),
    .bani200(i1_count), .bani500(i0_count), .sum(bills_to_sum_1_sum));
  mux_4in16bit mux_4in16bit_1 (
    .I0(registru_16_incarcare0_1_iesire), .I1(registru_16_incarcare1_1_iesire),
    .I2(registru_16_incarcare2_1_iesire), .I3(registru_16_incarcare3_1_iesire), .S(mux_2in2bit_3_y),
    .Y(mux_4in16bit_1_y));
  mux_3in16bit mux_3in16bit_1 (
    .I0(optiuni_retragere_suma_1_suma), .I1(bills_to_sum_1_sum), .I2(bcd_to_binary_1_bin),
    .S(uc_1_sel_val16), .Y(mux_3in16bit_1_y));
  mux_2in2bit mux_2in2bit_2 (.I0(PIN_PRINCIPAL_iesire), .I1(PIN_TR_iesire), .S(uc_1_sel_pin), .Y(mux_2in2bit_2_y));
  mux_4in16bit mux_4in16bit_2 (
    .I0(registru_16_incarcare0_1_iesire), .I1(registru_16_incarcare1_1_iesire),
    .I2(registru_16_incarcare2_1_iesire), .I3(registru_16_incarcare3_1_iesire), .S(mux_2in2bit_2_y),
    .Y(mux_4in16bit_2_y));
  demux_2out1bit demux_2out1bit_1 (.I(uc_1_we2), .S(uc_1_sel_pin), .Y0(demux_2out1bit_1_y0), .Y1(demux_2out1bit_1_y1));
  comparator_egalitate_v2 comparator_egalitate_v2_1 (
    .A0(i0_count), .A1(i1_count), .A2(i2_count), .A3(i3_count), .B0(registru_pin_3_1_i0),
    .B1(registru_pin_3_1_i1), .B2(registru_pin_3_1_i2), .B3(registru_pin_3_1_i3),
    .i(comparator_egalitate_v2_1_i));
  comparator_egalitate_v2 comparator_egalitate_v2_2 (
    .A0(i0_count), .A1(i1_count), .A2(i2_count), .A3(i3_count), .B0(registru_pin_2_1_i0),
    .B1(registru_pin_2_1_i1), .B2(registru_pin_2_1_i2), .B3(registru_pin_2_1_i3),
    .i(comparator_egalitate_v2_2_i));
  comparator_egalitate_v2 comparator_egalitate_v2_3 (
    .A0(i0_count), .A1(i1_count), .A2(i2_count), .A3(i3_count), .B0(registru_pin_1_1_i0),
    .B1(registru_pin_1_1_i1), .B2(registru_pin_1_1_i2), .B3(registru_pin_1_1_i3),
    .i(comparator_egalitate_v2_3_i));
  comparator_egalitate_v2 comparator_egalitate_v2_4 (
    .A0(i0_count), .A1(i1_count), .A2(i2_count), .A3(i3_count), .B0(registru_pin_0_1_i0),
    .B1(registru_pin_0_1_i1), .B2(registru_pin_0_1_i2), .B3(registru_pin_0_1_i3),
    .i(comparator_egalitate_v2_4_i));
  mux_2in2bit mux_2in2bit_3 (.I0(PIN_PRINCIPAL_iesire), .I1(PIN_TR_iesire), .S(uc_1_sel_pin), .Y(mux_2in2bit_3_y));
  sumator_scazator_16b sumator_scazator_16b_1 (
    .a(mux_4in16bit_1_y), .b(mux_3in16bit_1_y), .op(uc_1_op_ad_sc), .enable(uc_1_en_ad_sc),
    .c(sumator_scazator_16b_1_c));
  or or_1 (or_1_out, comparator_egalitate_v2_1_i, comparator_egalitate_v2_2_i, comparator_egalitate_v2_3_i, comparator_egalitate_v2_4_i);
  registru_2_incarcare PIN_PRINCIPAL (
    .clk(CLK_out), .we(demux_2out1bit_1_y0), .incarcare(demux_2out2bit_1_y0), .iesire(PIN_PRINCIPAL_iesire));
  registru_2_incarcare PIN_TR (
    .clk(CLK_out), .we(demux_2out1bit_1_y1), .incarcare(demux_2out2bit_1_y1), .iesire(PIN_TR_iesire));
  codificator_4in2out codificator_4in2out_1 (
    .I3(comparator_egalitate_v2_1_i), .I2(comparator_egalitate_v2_2_i), .I1(comparator_egalitate_v2_3_i),
    .I0(comparator_egalitate_v2_4_i), .iesire(codificator_4in2out_1_iesire));
  comparator_sold_suma comparator_sold_suma_1 (
    .data1(mux_4in16bit_2_y), .data2(mux_3in16bit_1_y), .i(comparator_sold_suma_1_i));
  binary_to_bcd binary_to_bcd_1 (
    .bin(mux_4in16bit_2_y), .bcd0(binary_to_bcd_1_bcd0), .bcd1(binary_to_bcd_1_bcd1),
    .bcd2(binary_to_bcd_1_bcd2), .bcd3(binary_to_bcd_1_bcd3), .bcd4(binary_to_bcd_1_bcd4));
  demux_2out2bit demux_2out2bit_1 (
    .I(codificator_4in2out_1_iesire), .S(uc_1_sel_pin), .Y0(demux_2out2bit_1_y0), .Y1(demux_2out2bit_1_y1));
  or or_2 (or_2_out, DELETE_EXIT, uc_1_clr_nr);
  mux_for_cash_reg mux_for_cash_reg_1 (
    .alg10(distribuitor_bani_1_rest10), .alg20(distribuitor_bani_1_rest20),
    .alg50(distribuitor_bani_1_rest50), .alg100(distribuitor_bani_1_rest100),
    .alg200(distribuitor_bani_1_rest200), .alg500(distribuitor_bani_1_rest500),
    .dep10(sum_nr_bills_1_newreg10), .dep20(sum_nr_bills_1_newreg20), .dep50(sum_nr_bills_1_newreg50),
    .dep100(sum_nr_bills_1_newreg100), .dep200(sum_nr_bills_1_newreg200), .dep500(sum_nr_bills_1_newreg500),
    .sel(uc_1_sel_w_in), .reg10(mux_for_cash_reg_1_reg10), .reg20(mux_for_cash_reg_1_reg20),
    .reg50(mux_for_cash_reg_1_reg50), .reg100(mux_for_cash_reg_1_reg100), .reg200(mux_for_cash_reg_1_reg200),
    .reg500(mux_for_cash_reg_1_reg500));
  sum_nr_bills sum_nr_bills_1 (
    .cashreg10(cash_register_1_cashreg10), .cashreg20(cash_register_1_cashreg20),
    .cashreg50(cash_register_1_cashreg50), .cashreg100(cash_register_1_cashreg100),
    .cashreg200(cash_register_1_cashreg200), .cashreg500(cash_register_1_cashreg500),
    .bani10(numarator_0_9_1_count), .bani20(numarator_0_9_2_count), .bani50(i3_count), .bani100(i2_count),
    .bani200(i1_count), .bani500(i0_count), .newreg10(sum_nr_bills_1_newreg10),
    .newreg20(sum_nr_bills_1_newreg20), .newreg50(sum_nr_bills_1_newreg50),
    .newreg100(sum_nr_bills_1_newreg100), .newreg200(sum_nr_bills_1_newreg200),
    .newreg500(sum_nr_bills_1_newreg500));
  cash_register cash_register_1 (
    .clk(CLK_out), .we(uc_1_we_bank), .rest10(mux_for_cash_reg_1_reg10), .rest20(mux_for_cash_reg_1_reg20),
    .rest50(mux_for_cash_reg_1_reg50), .rest100(mux_for_cash_reg_1_reg100),
    .rest200(mux_for_cash_reg_1_reg200), .rest500(mux_for_cash_reg_1_reg500),
    .cashreg10(cash_register_1_cashreg10), .cashreg20(cash_register_1_cashreg20),
    .cashreg50(cash_register_1_cashreg50), .cashreg100(cash_register_1_cashreg100),
    .cashreg200(cash_register_1_cashreg200), .cashreg500(cash_register_1_cashreg500));
  UC uc_1 (
    .CLOCK(CLK_out), .RESET(DELETE_EXIT), .OK(OK), .SW1(sw1), .SW0(sw0), .PIN_OK(or_1_out),
    .ENOUGH_ACC(comparator_sold_suma_1_i), .ENOUGH_BANK(comparator_sold_suma_2_i),
    .ERR_DISTR(distribuitor_bani_1_eroare), .DONE_DISTR(distribuitor_bani_1_done), .WE2(uc_1_we2),
    .SEL_PIN(uc_1_sel_pin), .SEL_SSD(uc_1_sel_ssd), .SEL_VAL16(uc_1_sel_val16), .EN_DISTR(uc_1_en_distr),
    .OP_AD_SC(uc_1_op_ad_sc), .EN_AD_SC(uc_1_en_ad_sc), .WE16(uc_1_we16), .SEL_W_IN(uc_1_sel_w_in),
    .WE_BANK(uc_1_we_bank), .CLR_NR(uc_1_clr_nr), .EN_NR2(uc_1_en_nr2), .ERROR(ERROR),
    .insertPIN(Insert_PIN), .selectOP(selectOP), .OP_FIN(OP_FIN), .insertSUM(InsertSUM),
    .insertBILLS(InsertBILLS), .interogare(interogare), .retragere(retragere), .depunere(depunere),
    .transfer(transfer), .calculating(calculating));
  distribuitor_bani distribuitor_bani_1 (
    .clk(CLK_out), .enb(uc_1_en_distr), .suma(optiuni_retragere_suma_1_suma),
    .cashreg10(cash_register_1_cashreg10), .cashreg20(cash_register_1_cashreg20),
    .cashreg50(cash_register_1_cashreg50), .cashreg100(cash_register_1_cashreg100),
    .cashreg200(cash_register_1_cashreg200), .cashreg500(cash_register_1_cashreg500),
    .bani10(distribuitor_bani_1_bani10), .bani20(distribuitor_bani_1_bani20),
    .bani50(distribuitor_bani_1_bani50), .bani100(distribuitor_bani_1_bani100),
    .bani200(distribuitor_bani_1_bani200), .bani500(distribuitor_bani_1_bani500),
    .rest10(distribuitor_bani_1_rest10), .rest20(distribuitor_bani_1_rest20),
    .rest50(distribuitor_bani_1_rest50), .rest100(distribuitor_bani_1_rest100),
    .rest200(distribuitor_bani_1_rest200), .rest500(distribuitor_bani_1_rest500),
    .eroare(distribuitor_bani_1_eroare), .done(distribuitor_bani_1_done));
  cash_register_sold cash_register_sold_1 (
    .i10(cash_register_1_cashreg10), .i20(cash_register_1_cashreg20), .i50(cash_register_1_cashreg50),
    .i100(cash_register_1_cashreg100), .i200(cash_register_1_cashreg200), .i500(cash_register_1_cashreg500),
    .sold(cash_register_sold_1_sold));
  Clock CLK (.out(CLK_out));
  comparator_sold_suma comparator_sold_suma_2 (
    .data1(cash_register_sold_1_sold), .data2(optiuni_retragere_suma_1_suma), .i(comparator_sold_suma_2_i));
  bcd_to_7seg bcd_to_7seg_1 (.BCD(mux_ssd4_1_y), .seg(ssd5));
  mux_ssd4 mux_ssd4_1 (.i0(mux_in_or0_4bit_2_y), .i2(distribuitor_bani_1_bani10), .sel(uc_1_sel_ssd), .y(mux_ssd4_1_y));
  _7_Segment_Display #(.decimalPoint("false")) u_7_segment_display_1 (
    .g(undriven), .f(undriven_3), .a(undriven_5), .b(undriven_7), .e(undriven_2), .d(undriven_4),
    .c(undriven_6));
  bcd_to_7seg bcd_to_7seg_2 (.BCD(mux_ssd_1_y), .seg(ssd4));
  mux_ssd mux_ssd_1 (
    .i0(mux_in_or0_4bit_1_y), .i1(binary_to_bcd_1_bcd4), .i2(distribuitor_bani_1_bani20), .sel(uc_1_sel_ssd),
    .y(mux_ssd_1_y));
  bcd_to_binary bcd_to_binary_2 (.i0(i0_count), .i1(i1_count), .i2(i2_count), .i3(i3_count), .bin(bcd_to_binary_2_bin));
  _7_Segment_Display #(.decimalPoint("false")) u_7_segment_display_2 (
    .g(undriven_8), .f(undriven_10), .a(undriven_12), .b(undriven_14), .e(undriven_9), .d(undriven_11),
    .c(undriven_13));
  _7_Segment_Display #(.decimalPoint("false")) u_7_segment_display_3 (
    .g(undriven_15), .f(undriven_17), .a(undriven_19), .b(undriven_21), .e(undriven_16), .d(undriven_18),
    .c(undriven_20));
  bcd_to_7seg bcd_to_7seg_3 (.BCD(mux_ssd_2_y), .seg(ssd3));
  mux_ssd mux_ssd_2 (
    .i0(i3_count), .i1(binary_to_bcd_1_bcd3), .i2(distribuitor_bani_1_bani50), .sel(uc_1_sel_ssd),
    .y(mux_ssd_2_y));
  mux_in_or0_4bit mux_in_or0_4bit_1 (.I(numarator_0_9_2_count), .S(uc_1_en_nr2), .Y(mux_in_or0_4bit_1_y));
  mux_in_or0_4bit mux_in_or0_4bit_2 (.I(numarator_0_9_1_count), .S(uc_1_en_nr2), .Y(mux_in_or0_4bit_2_y));
  _7_Segment_Display #(.decimalPoint("false")) u_7_segment_display_4 (
    .g(undriven_22), .f(undriven_24), .a(undriven_26), .b(undriven_28), .e(undriven_23), .d(undriven_25),
    .c(undriven_27));
  bcd_to_7seg bcd_to_7seg_4 (.BCD(mux_ssd_3_y), .seg(ssd2));
  mux_ssd mux_ssd_3 (
    .i0(i2_count), .i1(binary_to_bcd_1_bcd2), .i2(distribuitor_bani_1_bani100), .sel(uc_1_sel_ssd),
    .y(mux_ssd_3_y));
  bcd_to_7seg bcd_to_7seg_5 (.BCD(mux_ssd_4_y), .seg(ssd1));
  mux_ssd mux_ssd_4 (
    .i0(i1_count), .i1(binary_to_bcd_1_bcd1), .i2(distribuitor_bani_1_bani200), .sel(uc_1_sel_ssd),
    .y(mux_ssd_4_y));
  _7_Segment_Display #(.decimalPoint("false")) u_7_segment_display_5 (
    .g(undriven_29), .f(undriven_31), .a(undriven_33), .b(undriven_35), .e(undriven_30), .d(undriven_32),
    .c(undriven_34));
  bcd_to_7seg bcd_to_7seg_6 (.BCD(mux_ssd_5_y), .seg(ssd0));
  mux_ssd mux_ssd_5 (
    .i0(i0_count), .i1(binary_to_bcd_1_bcd0), .i2(distribuitor_bani_1_bani500), .sel(uc_1_sel_ssd),
    .y(mux_ssd_5_y));
  _7_Segment_Display #(.decimalPoint("false")) u_7_segment_display_6 (
    .g(undriven_36), .f(undriven_38), .a(undriven_40), .b(undriven_42), .e(undriven_37), .d(undriven_39),
    .c(undriven_41));
  optiuni_retragere_suma optiuni_retragere_suma_1 (
    .ret500(ret500), .ret200(ret200), .ret100(ret100), .ret50(ret50), .ret20(ret20), .ret10(ret10),
    .rets(ret_alta_suma), .alta_suma(bcd_to_binary_2_bin), .suma(optiuni_retragere_suma_1_suma));

  // Notes on the sheet:
  //   10
  //   20
  //   50
  //   100
  //   200
  //   500
  //   10
  //   20
  //   50
  //   100
  //   200
  //   500
endmodule

module test (
  input  SW1_OPTIUNI,
  input  SW0_OPTIUNI,
  input  retragere_alta_suma,
  input  retragere_10,
  input  retragere_20,
  input  retragere_50,
  input  retragere_100,
  input  retragere_200,
  input  retragere_500,
  input  _10,
  input  _20,
  input  _50,
  input  _100,
  input  _200,
  input  _500,
  output out_16,
  output out_17,
  output out_18,
  output out_19,
  output out_20,
  output out_21,
  output out_22,
  output out_23,
  output out_24,
  output out_25,
  output out_26
);

  wire DELETE_EXIT_out, OK_out;
  wire [6:0] main_1_ssd0, main_1_ssd1, main_1_ssd2, main_1_ssd3, main_1_ssd4, main_1_ssd5;

  Clock clock_1 ();  // open: out
  Button DELETE_EXIT (.out(DELETE_EXIT_out));
  Button OK (.out(OK_out));
  main main_1 (
    .ret_alta_suma(retragere_alta_suma), .DELETE_EXIT(DELETE_EXIT_out), .ret10(retragere_10), .OK(OK_out),
    .ret20(retragere_20), .sw1(SW1_OPTIUNI), .sw0(SW0_OPTIUNI), .ret50(retragere_50), .ret100(retragere_100),
    .ret200(retragere_200), .ret500(retragere_500), .nr5(_10), .nr4(_20), .nr3(_50), .nr2(_100), .nr1(_200),
    .nr0(_500), .ERROR(out_16), .Insert_PIN(out_17), .selectOP(out_18), .OP_FIN(out_19), .InsertSUM(out_20),
    .InsertBILLS(out_21), .interogare(out_22), .retragere(out_23), .depunere(out_24), .transfer(out_25),
    .calculating(out_26), .ssd5(main_1_ssd5), .ssd4(main_1_ssd4), .ssd3(main_1_ssd3), .ssd2(main_1_ssd2),
    .ssd1(main_1_ssd1), .ssd0(main_1_ssd0));
  _7_Segment_Display #(.decimalPoint("false")) u_7_segment_display_1 (
    .g(main_1_ssd5[0]), .f(main_1_ssd5[1]), .a(main_1_ssd5[6]), .b(main_1_ssd5[5]), .e(main_1_ssd5[2]),
    .d(main_1_ssd5[3]), .c(main_1_ssd5[4]));
  _7_Segment_Display #(.decimalPoint("false")) u_7_segment_display_2 (
    .g(main_1_ssd4[0]), .f(main_1_ssd4[1]), .a(main_1_ssd4[6]), .b(main_1_ssd4[5]), .e(main_1_ssd4[2]),
    .d(main_1_ssd4[3]), .c(main_1_ssd4[4]));
  _7_Segment_Display #(.decimalPoint("false")) u_7_segment_display_3 (
    .g(main_1_ssd3[0]), .f(main_1_ssd3[1]), .a(main_1_ssd3[6]), .b(main_1_ssd3[5]), .e(main_1_ssd3[2]),
    .d(main_1_ssd3[3]), .c(main_1_ssd3[4]));
  _7_Segment_Display #(.decimalPoint("false")) u_7_segment_display_4 (
    .g(main_1_ssd2[0]), .f(main_1_ssd2[1]), .a(main_1_ssd2[6]), .b(main_1_ssd2[5]), .e(main_1_ssd2[2]),
    .d(main_1_ssd2[3]), .c(main_1_ssd2[4]));
  _7_Segment_Display #(.decimalPoint("false")) u_7_segment_display_5 (
    .g(main_1_ssd1[0]), .f(main_1_ssd1[1]), .a(main_1_ssd1[6]), .b(main_1_ssd1[5]), .e(main_1_ssd1[2]),
    .d(main_1_ssd1[3]), .c(main_1_ssd1[4]));
  _7_Segment_Display #(.decimalPoint("false")) u_7_segment_display_6 (
    .g(main_1_ssd0[0]), .f(main_1_ssd0[1]), .a(main_1_ssd0[6]), .b(main_1_ssd0[5]), .e(main_1_ssd0[2]),
    .d(main_1_ssd0[3]), .c(main_1_ssd0[4]));

  // Notes on the sheet:
  //   (depunere bancnote)
  //   10
  //   20
  //   50
  //   100
  //        200
  //   500
  //   (bancnote depuse/retrase)
endmodule

// VHDL entity numarator_0_9, as the project stores it:
--------------------------------------------------------------------------------
-- Project :
-- File    :
-- Autor   :
-- Date    :
--
--------------------------------------------------------------------------------
-- Description :
--
--------------------------------------------------------------------------------
LIBRARY ieee;
USE ieee.std_logic_1164.all;
USE ieee.std_logic_UNSIGNED.all;
ENTITY numarator_0_9 IS
  PORT (
ENABLE, RESET, CLK : IN STD_LOGIC;
  COUNT: OUT STD_LOGIC_VECTOR (3 DOWNTO 0));
END numarator_0_9;

--------------------------------------------------------------------------------
--Complete your VHDL description below
--------------------------------------------------------------------------------

architecture behavioral of numarator_0_9 is
    
begin
process (clk, reset)
variable nr: std_logic_vector(3 downto 0) := (others => '0');
    begin
        if reset = '1' then
            nr := (others => '0');
        elsif rising_edge(clk) then
            if enable = '1' then
                if nr = "1001" then
                    nr := (others => '0');
                else
                    nr := nr + 1;
                end if;
            end if;
        end if; 
    count <= nr;
    end process;
   
end architecture;

// VHDL entity sumator_scazator_16b, as the project stores it:
--------------------------------------------------------------------------------
-- Project :
-- File    :
-- Autor   :
-- Date    :
--
--------------------------------------------------------------------------------
-- Description :
--
--------------------------------------------------------------------------------

library ieee;
use ieee.std_logic_1164.all;
use ieee.std_logic_unsigned.all;
--use ieee.numeric_std.all;

entity sumator_scazator_16b is
  port (
    a, b: in std_logic_vector(15 downto 0);
    op: in std_logic;
    enable: in std_logic;
    c: out std_logic_vector(15 downto 0)
  );
end entity sumator_scazator_16b;

architecture behavioral of sumator_scazator_16b is

begin 

  process (a, b, op, enable)
 	variable auxa: std_logic_vector(15 downto 0);
	variable auxb: std_logic_vector(15 downto 0);
	variable auxc: std_logic_vector(15 downto 0) := (others => '0');
  begin
  	auxa := a;
	auxb := b;
	
    if (enable = '1') then
      if (op = '1') then
        auxc := auxa + auxb;
      else
        auxc := auxa - auxb;
      end if;
    else
      auxc := (others => '0');
    end if;
    c <= auxc;
  end process;
end architecture behavioral;


-- op = '1' => adunare
-- op = '0' => scadere

--trebuie tinut cont ca are nevoie de enable dupa ce primeste a si b ca sa dea rezultetul corect pe c. Daca e enable prima data si apoi intrarile atunci nu va avea iesirea buna.

// VHDL entity codificator_4in2out, as the project stores it:
--------------------------------------------------------------------------------
-- Project :
-- File    :
-- Autor   :
-- Date    :
--
--------------------------------------------------------------------------------
-- Description :
--
--------------------------------------------------------------------------------

LIBRARY ieee;
USE ieee.std_logic_1164.all;

ENTITY codificator_4in2out IS
  PORT (
  		I3, I2, I1, I0: in std_logic;
  		iesire: out std_logic_vector (1 downto 0)
    );
END codificator_4in2out;

--------------------------------------------------------------------------------
--Complete your VHDL description below
--------------------------------------------------------------------------------

ARCHITECTURE TypeArchitecture OF codificator_4in2out IS
BEGIN

	process (I3, I2, I1, I0)
	begin

		if I0 = '1' then iesire <= "00";
		elsif I1 = '1' then iesire <= "01";
		elsif I2 = '1' then iesire <= "10";
		else iesire <= "11";
		end if;
	end process;

END TypeArchitecture;


--daca nu se activeaza nicio iesire atunci rezultatul va fi "11"

// VHDL entity demux_2out2bit, as the project stores it:
--------------------------------------------------------------------------------
-- Project :
-- File    :
-- Autor   :
-- Date    :
--
--------------------------------------------------------------------------------
-- Description :
--
--------------------------------------------------------------------------------

LIBRARY ieee;
USE ieee.std_logic_1164.all;

ENTITY demux_2out2bit IS
  PORT (
 		I: in std_logic_vector (1 downto 0);
  		S: in std_logic;
  		Y0, Y1: out std_logic_vector (1 downto 0)
    );
END demux_2out2bit;

--------------------------------------------------------------------------------
--Complete your VHDL description below
--------------------------------------------------------------------------------

ARCHITECTURE TypeArchitecture OF demux_2out2bit IS

BEGIN
process (S, I)
	begin
	if S = '0'THEN 
		Y0 <= I;
		Y1 <= "00";
	else 
		Y0 <= "00";
		Y1 <= I;
	end if;
end process;


END TypeArchitecture;

// VHDL entity mux_2in2bit, as the project stores it:
--------------------------------------------------------------------------------
-- Project :
-- File    :
-- Autor   :
-- Date    :
--
--------------------------------------------------------------------------------
-- Description :
--
--------------------------------------------------------------------------------

LIBRARY ieee;
USE ieee.std_logic_1164.all;

ENTITY mux_2in2bit IS
  PORT (
  		I0, I1: in std_logic_vector (1 downto 0);
  		S: in std_logic;
  		Y: out std_logic_vector (1 downto 0)
    );
END mux_2in2bit;

--------------------------------------------------------------------------------
--Complete your VHDL description below
--------------------------------------------------------------------------------

ARCHITECTURE TypeArchitecture OF mux_2in2bit IS

BEGIN
process (S, I0, I1)	--se va schimba iesirea la modificarea intrarilor
	begin
	if S = '0'THEN Y <= I0;
	else Y <= I1;
	end if;
end process;


END TypeArchitecture;

// VHDL entity mux_4in16bit, as the project stores it:
--------------------------------------------------------------------------------
-- Project :
-- File    :
-- Autor   :
-- Date    :
--
--------------------------------------------------------------------------------
-- Description :
--
--------------------------------------------------------------------------------

LIBRARY ieee;
USE ieee.std_logic_1164.all;

ENTITY mux_4in16bit IS
  PORT (
  		I0, I1, I2, I3: in std_logic_vector (15 downto 0);
  		S: in std_logic_vector (1 downto 0);
  		Y: out std_logic_vector (15 downto 0)
    );
END mux_4in16bit;

--------------------------------------------------------------------------------
--Complete your VHDL description below
--------------------------------------------------------------------------------

ARCHITECTURE TypeArchitecture OF mux_4in16bit IS

BEGIN
process (S, I0, I1, I2, I3)	--se va schimba iesirea la modificarea intrarilor
	begin
	if S = "00" THEN Y <= I0;
	elsif S = "01"THEN Y <= I1;
	elsif S = "10"THEN Y <= I2;
	else Y <= I3;
	end if;
end process;


END TypeArchitecture;

// VHDL entity registru_16_incarcare0, as the project stores it:
--------------------------------------------------------------------------------
-- Project :
-- File    :
-- Autor   :
-- Date    :
--
--------------------------------------------------------------------------------
-- Description :
--
--------------------------------------------------------------------------------

LIBRARY ieee;
USE ieee.std_logic_1164.all;

ENTITY registru_16_incarcare0 IS
  PORT (
  		clk: in std_logic;
  		we: in std_logic;
  		incarcare: in std_logic_vector (15 downto 0);	
 		iesire: out std_logic_vector ( 15 downto 0)
    );
END registru_16_incarcare0;

--------------------------------------------------------------------------------
--Complete your VHDL description below
--------------------------------------------------------------------------------

ARCHITECTURE TypeArchitecture OF registru_16_incarcare0 IS

BEGIN
	process (clk)
	variable reg: std_logic_vector(15 downto 0):=x"04E2"; --1250
	begin
		if clk'event and clk = '1' then 
			if we = '1' then
				reg := incarcare;
			else reg:=reg;
			end if;
		end if;
		iesire<= reg;
	end process;

END TypeArchitecture;


--nu merge initializat incarcare in entitate

// VHDL entity registru_PIN_0, as the project stores it:
--------------------------------------------------------------------------------
-- Project :
-- File    :
-- Autor   :
-- Date    :
--
--------------------------------------------------------------------------------
-- Description :
--
--------------------------------------------------------------------------------

LIBRARY ieee;
USE ieee.std_logic_1164.all;

ENTITY registru_PIN_0 IS
  PORT (
  		clk: in std_logic;
 		I0, I1, I2, I3: out std_logic_vector (3 downto 0) --4 iesiri fiecare de cate 4 biti
    );
END registru_PIN_0;

--------------------------------------------------------------------------------
--Complete your VHDL description below
--------------------------------------------------------------------------------

ARCHITECTURE TypeArchitecture OF registru_PIN_0 IS

	signal valoare_stocata: std_logic_vector (15 downto 0) := "0010010001101000";	--pinul din primul registru va fi 2468

BEGIN
	process (clk)
	begin
		if clk'event and clk = '1' then 
			I0 <= valoare_stocata (3 downto 0);
			I1 <= valoare_stocata (7 downto 4);
			I2 <= valoare_stocata (11 downto 8);
			I3 <= valoare_stocata (15 downto 12);
		end if;
	end process;


END TypeArchitecture;

--mi se pare ca clockul aici e degeaba

// VHDL entity UC, as the project stores it:
--------------------------------------------------------------------------------
-- Project :
-- File    :
-- Autor   :
-- Date    :
--
--------------------------------------------------------------------------------
-- Description :
--
--------------------------------------------------------------------------------

LIBRARY ieee;
USE ieee.std_logic_1164.all;

ENTITY UC IS
  PORT (
  		----intrari:
  		--butane/switchuri
  		CLOCK, RESET: in std_logic;
  		OK: in std_logic;
  		SW1, SW0: in std_logic;
		
  		--semnale interne
  		PIN_OK: in std_logic;
  		ENOUGH_ACC: in std_logic;
  		ENOUGH_BANK: in std_logic;
  		ERR_DISTR: in std_logic;
  		DONE_DISTR: in std_logic;


  		----iesiri:
  		--semnale interne
  		WE2: out std_logic;
  		SEL_PIN: out std_logic;
  		SEL_SSD: out std_logic_vector(1 downto 0);		--nu cred ca e nevoie de initializare
  		SEL_VAL16: out std_logic_vector(1 downto 0);		--nu cred ca e nevoie de initializare
  		EN_DISTR:out std_logic;
  		OP_AD_SC: out std_logic;						--nu cred ca e nevoie de initializare
  		EN_AD_SC: out std_logic;
  		WE16: out std_logic;
  		SEL_W_IN: out std_logic;						--nu cred ca e nevoie de initializare
  		WE_BANK:out std_logic;
  		CLR_NR: out std_logic;
  		EN_NR2: out std_logic;
  		

		--leduri
		ERROR:out std_logic;
		insertPIN: out std_logic;
		selectOP: out std_logic;
		OP_FIN: out std_logic;
		insertSUM: out std_logic;
		insertBILLS: out std_logic;
		interogare: out std_logic;
		retragere: out std_logic;
		depunere: out std_logic;
		transfer: out std_logic;
		calculating: out std_logic
    );
END UC;

--------------------------------------------------------------------------------
--Complete your VHDL description below

--------------------------------------------------------------------------------

ARCHITECTURE arhitectura_1 OF UC IS
	type STARE_T is (ST0, ST1, ST2, ST3, ST4, ST5, ST6, ST7, ST8, ST9, ST10, ST11, ST12, ST13, ST14, ST15, ST16, ST17, ST18, ST19, ST20, ST21, ST22, ST23, ST24);
	signal STARE, NXSTARE: STARE_T;
BEGIN
	ACTUALIZEAZA_STARE: process (RESET, CLOCK) 
	begin
		 if (RESET = '1') then
		 STARE <= ST0; 
		 elsif CLOCK'event and CLOCK = '1' then
		 STARE <= NXSTARE; 
		 end if; 
	end process ACTUALIZEAZA_STARE;

	TRANSITIONS: process (STARE,ok, SW1, SW0, PIN_OK, ENOUGH_ACC,ENOUGH_BANK, ERR_DISTR, DONE_DISTR) 
	begin
		 -- SEMNALE INTERNE
		WE2 <= '0';
		SEL_PIN <= '0';
		EN_DISTR <= '0';
		EN_AD_SC <= '0';
		WE16 <= '0';
		WE_BANK <= '0';
		CLR_NR <= '0';
		EN_NR2 <= '0';
		
		

		--LEDURI
		ERROR <= '0';
		insertPIN <= '0';
		selectOP <='0';
		OP_FIN <= '0';
		insertSUM <= '0';
		insertBILLS <= '0';
		interogare <= '0';
		retragere <= '0';
		depunere <= '0';
		transfer <= '0';
		calculating <= '0';
		
		case STARE is
		 	when ST0 =>
		 		insertPIN <= '1';
		 		SEL_SSD<="00";
		 		if OK = '1' then NXSTARE <= ST1;
		 		else NXSTARE <= ST0;
		 		end if;
				
			 when ST1 => 
			 	if PIN_OK = '1' then 
			 		SEL_PIN <= '0';
			 		WE2 <= '1';		--scriu in registrul in care tin nuamrul registrului in care e pinul de care ne folosim
			 		NXSTARE <= ST2;
			 	else 
			 		ERROR <= '1';
			 		NXSTARE <= ST0;
			 	end if;
			 	
		 	when ST2 =>
		 		selectOP <= '1';
		 		if OK = '1' then 
		 			if SW1 = '0' and SW0 = '0' then 
		 				NXSTARE <= ST3;
		 			elsif SW1 = '0' and SW0 = '1' then 
		 				NXSTARE <= ST4;
		 			elsif SW1 = '1' and SW0 = '0' then 
		 				NXSTARE <= ST11;
		 			elsif SW1 = '1' and SW0 = '1' then 
		 				NXSTARE <= ST16;
		 			end if;

		 		else NXSTARE <= ST2;
		 		end if;

----------incepe INTEROGARE
		 	when ST3 =>				
		 		interogare <= '1';
		 		CLR_NR <= '1';
		 		SEL_PIN <= '0';
		 		SEL_SSD<="01";
		 		OP_FIN <= '1';
		 		if OK = '1' then 
		 			SEL_SSD <= "11";
		 			NXSTARE <= ST2;
		 		else NXSTARE <= ST3;
		 		end if;
-----------se termina INTEROGARE

----------incepe RETRAGERE
		 	when ST4 => 
		 		retragere <= '1';
		 		CLR_NR <= '1';
		 		insertSUM<= '1';
		 		SEL_SSD <= "00";
		 		NXSTARE <= ST5;

		 	when ST5 => 
		 		retragere <= '1';
		 		insertSUM<= '1';
		 		SEL_SSD <= "00";
		 		if ok = '1' then 
		 			NXSTARE <= ST6;
		 		else
		 			NXSTARE <= ST5;
		 		end if;

		 	when ST6 =>
		 		retragere <= '1';
		 		SEL_PIN <='0';
		 		SEL_VAL16 <="00";
		 		if ENOUGH_ACC = '1' and ENOUGH_BANK = '1' then
		 			EN_DISTR <= '1';
		 			NXSTARE <= ST7;
		 		else 
		 			ERROR <= '1';
		 			NXSTARE <= ST4;
		 		end if;	

		 	when ST7 =>
		 		retragere <= '1';
		 		if ERR_DISTR = '1' then 
		 			ERROR <= '1';
		 			NXSTARE <= ST4;
		 		else 
		 			if DONE_DISTR = '1' then 
		 				NXSTARE <= ST8;
		 			else 
		 				calculating <= '1';
		 				NXSTARE <= ST7;
		 			end if;
		 		end if;

		 	when ST8 => 
		 		retragere <= '1';
		 		SEL_PIN <= '0';
		 		SEL_VAL16 <= "00";
		 		OP_AD_SC <= '0';
		 		EN_AD_SC <= '1';
		 		WE16 <= '1';
		 		NXSTARE <= ST9;

		 	when ST9 =>
		 		retragere <= '1';
		 		SEL_W_IN <= '0';
		 		WE_BANK <= '1';
		 		NXSTARE <= ST10;

		 	when ST10 =>
		 		retragere <= '1';
		 		CLR_NR <= '1';
		 		SEL_SSD <= "10";
		 		OP_FIN <= '1';
		 		if ok = '1' then 
		 			SEL_SSD <= "11";
		 			NXSTARE <= ST2;
		 		else 
		 			NXSTARE <= ST10;
		 		end if;
-----------se termina RETRAGERE

----------incepe DEPUNERE
			when ST11 => 
				depunere <= '1';
				CLR_NR <= '1';
				SEL_SSD <= "00";
				insertBILLS <= '1';
				EN_NR2 <= '1';
				NXSTARE <= ST12;

			when ST12 => 
				depunere <= '1';
		 		SEL_SSD <= "00";
		 		insertBILLS <= '1';
				EN_NR2 <= '1';
				if ok = '1' then 
					SEL_SSD <= "11";
					NXSTARE <= ST13;
				else 
					NXSTARE <= ST12;
				end if;

			when ST13 =>
				depunere <= '1';
				SEL_PIN <= '0';
				SEL_VAL16 <= "01";
				OP_AD_SC <= '1';
				EN_AD_SC <= '1';
				WE16 <= '1';
				NXSTARE <= ST14;

			when ST14 => 
				depunere <= '1';
				SEL_W_IN <= '1';
				WE_BANK <= '1';
				NXSTARE <= ST15;

			when ST15 => 
				depunere <= '1';
				OP_FIN <= '1';
				if ok = '1' then 
					NXSTARE <= ST2;
				else 
					NXSTARE <= ST15;
				end if;
-----------se termina DEPUNERE

----------incepe TRANSFER
			when ST16 => 
				transfer <= '1';
				insertPIN <= '1';
				CLR_NR <= '1';
				SEL_SSD <= "00";
				NXSTARE <= ST17;

			when ST17 =>
				transfer <= '1';
				insertPIN <= '1';
				SEL_SSD <= "00";
				if ok = '1' then 
					NXSTARE <= ST18;
				else 
					NXSTARE <= ST17;
				end if;

			when ST18 => 
				transfer <= '1';
				if PIN_OK = '1' then
					SEL_PIN <= '1';
					WE2 <= '1';
					NXSTARE <= ST19;
				else 
					ERROR <= '1';
					NXSTARE <= ST16;
				end if;

			when ST19 =>
				transfer <= '1';
				CLR_NR <= '1';
				SEL_SSD <= "00";
				insertSUM <= '1';
				NXSTARE <= ST20;

			when ST20 => 
				transfer <= '1';
				SEL_SSD <= "00";
				insertSUM <= '1';
				if ok = '1' then 
					NXSTARE <= ST21;
				else 
					NXSTARE <= ST20;
				end if;

			when ST21 => 
				transfer <= '1';
				SEL_PIN <= '0';
				SEL_VAL16 <= "10";
				if ENOUGH_ACC = '1' then 
					NXSTARE <= ST22;
				else 
					ERROR <= '1';
					NXSTARE <= ST20;
				end if;
				
			when ST22 => 
				transfer <= '1';
				SEL_PIN <= '0';
				SEL_VAL16 <= "10";
				OP_AD_SC <= '0';
				EN_AD_SC <= '1';
				WE16 <= '1';
				NXSTARE <= ST23;

			when ST23 => 
				transfer <= '1';
				SEL_PIN <= '1';
				SEL_VAL16 <= "10";
				OP_AD_SC <= '1';
				EN_AD_SC <= '1';
				WE16 <= '1';
				NXSTARE <= ST24;

			when ST24 =>
				transfer <= '1';
				OP_FIN <= '1';
				if ok = '1' then 
					SEL_SSD <= "11";
					NXSTARE <= ST2;
				else 
					NXSTARE <= ST24;
				end if;
-----------se termina TRANSFER
		 		
		end case; 
	end process TRANSITIONS; 


END arhitectura_1;

// VHDL entity registru_PIN_1, as the project stores it:
--------------------------------------------------------------------------------
-- Project :
-- File    :
-- Autor   :
-- Date    :
--
--------------------------------------------------------------------------------
-- Description :
--
--------------------------------------------------------------------------------

LIBRARY ieee;
USE ieee.std_logic_1164.all;

ENTITY registru_PIN_1 IS
  PORT (
  		clk: in std_logic;
 		I0, I1, I2, I3: out std_logic_vector (3 downto 0) --4 iesiri fiecare de cate 4 biti
    );
END registru_PIN_1;

--------------------------------------------------------------------------------
--Complete your VHDL description below
--------------------------------------------------------------------------------

ARCHITECTURE TypeArchitecture OF registru_PIN_1 IS

	signal valoare_stocata: std_logic_vector (15 downto 0) := "0111011001010100";	--pinul din al doilea registru va fi 7654

BEGIN
	process (clk)
	begin
		if clk'event and clk = '1' then 
			I0 <= valoare_stocata (3 downto 0);
			I1 <= valoare_stocata (7 downto 4);
			I2 <= valoare_stocata (11 downto 8);
			I3 <= valoare_stocata (15 downto 12);
		end if;
	end process;


END TypeArchitecture;

--mi se pare ca clockul aici e degeaba

// VHDL entity registru_PIN_2, as the project stores it:
--------------------------------------------------------------------------------
-- Project :
-- File    :
-- Autor   :
-- Date    :
--
--------------------------------------------------------------------------------
-- Description :
--
--------------------------------------------------------------------------------

LIBRARY ieee;
USE ieee.std_logic_1164.all;

ENTITY registru_PIN_2 IS
  PORT (
  		clk: in std_logic;
 		I0, I1, I2, I3: out std_logic_vector (3 downto 0) --4 iesiri fiecare de cate 4 biti
    );
END registru_PIN_2;

--------------------------------------------------------------------------------
--Complete your VHDL description below
--------------------------------------------------------------------------------

ARCHITECTURE TypeArchitecture OF registru_PIN_2 IS

	signal valoare_stocata: std_logic_vector (15 downto 0) := "0011001100110011";	--pinul din al treilea registru va fi 3333

BEGIN
	process (clk)
	begin
		if clk'event and clk = '1' then 
			I0 <= valoare_stocata (3 downto 0);
			I1 <= valoare_stocata (7 downto 4);
			I2 <= valoare_stocata (11 downto 8);
			I3 <= valoare_stocata (15 downto 12);
		end if;
	end process;


END TypeArchitecture;

--mi se pare ca clockul aici e degeaba

// VHDL entity registru_PIN_3, as the project stores it:
--------------------------------------------------------------------------------
-- Project :
-- File    :
-- Autor   :
-- Date    :
--
--------------------------------------------------------------------------------
-- Description :
--
--------------------------------------------------------------------------------

LIBRARY ieee;
USE ieee.std_logic_1164.all;

ENTITY registru_PIN_3 IS
  PORT (
  		clk: in std_logic;
 		I0, I1, I2, I3: out std_logic_vector (3 downto 0) --4 iesiri fiecare de cate 4 biti
    );
END registru_PIN_3;

--------------------------------------------------------------------------------
--Complete your VHDL description below
--------------------------------------------------------------------------------

ARCHITECTURE TypeArchitecture OF registru_PIN_3 IS

	signal valoare_stocata: std_logic_vector (15 downto 0) := "0000000100100011";	--pinul din al patrulea registru va fi 0123

BEGIN
	process (clk)
	begin
		if clk'event and clk = '1' then 
			I0 <= valoare_stocata (3 downto 0);
			I1 <= valoare_stocata (7 downto 4);
			I2 <= valoare_stocata (11 downto 8);
			I3 <= valoare_stocata (15 downto 12);
		end if;
	end process;


END TypeArchitecture;

--mi se pare ca clockul aici e degeaba

// VHDL entity comparator_egalitate_v2, as the project stores it:
--------------------------------------------------------------------------------
-- Project :
-- File    :
-- Autor   :
-- Date    :
--
--------------------------------------------------------------------------------
-- Description :
--
--------------------------------------------------------------------------------

LIBRARY ieee;
USE ieee.std_logic_1164.all;

ENTITY comparator_egalitate_v2 IS
  PORT (
		--enb: in std_logic;
  		A0, A1, A2, A3: in std_logic_vector(3 downto 0);
  		B0, B1, B2, B3: in std_logic_vector(3 downto 0);
  		i: out std_logic)
;
END comparator_egalitate_v2;

--------------------------------------------------------------------------------
--Complete your VHDL description below
--------------------------------------------------------------------------------

ARCHITECTURE TypeArchitecture OF comparator_egalitate_v2 IS

BEGIN
	process(A0, A1, A2, A3, B0, B1, B2, B3)
		begin
			i<= '0';
			if A0 = B0 AND A1 = B1 AND A2 = B2 AND A3 = B3 then i<='1';
			end if;
	end process;
END TypeArchitecture;

// VHDL entity registru_2_incarcare, as the project stores it:
--------------------------------------------------------------------------------
-- Project :
-- File    :
-- Autor   :
-- Date    :
--
--------------------------------------------------------------------------------
-- Description :
--
--------------------------------------------------------------------------------

LIBRARY ieee;
USE ieee.std_logic_1164.all;

ENTITY registru_2_incarcare IS
  PORT (
  		clk: in std_logic;
  		we: in std_logic;
  		incarcare: in std_logic_vector (1 downto 0);	
 		iesire: out std_logic_vector (1 downto 0)
    );
END registru_2_incarcare;

--------------------------------------------------------------------------------
--Complete your VHDL description below
--------------------------------------------------------------------------------

ARCHITECTURE TypeArchitecture OF registru_2_incarcare IS

BEGIN
	process (clk)
	variable reg: std_logic_vector(1 downto 0):="00";
	begin
		if clk'event and clk = '1' then 
			if we = '1' then
				reg := incarcare;
			else reg:=reg;
			end if;
		end if;
		iesire<= reg;
	end process;

END TypeArchitecture;

// VHDL entity demux_2out1bit, as the project stores it:
--------------------------------------------------------------------------------
-- Project :
-- File    :
-- Autor   :
-- Date    :
--
--------------------------------------------------------------------------------
-- Description :
--
--------------------------------------------------------------------------------

LIBRARY ieee;
USE ieee.std_logic_1164.all;

ENTITY demux_2out1bit IS
  PORT (
 		I: in std_logic;
  		S: in std_logic;
  		Y0, Y1: out std_logic
    );
END demux_2out1bit;

--------------------------------------------------------------------------------
--Complete your VHDL description below
--------------------------------------------------------------------------------

ARCHITECTURE TypeArchitecture OF demux_2out1bit IS

BEGIN
process (S, I)
	begin
	if S = '0'THEN 
		Y0 <= I;
		Y1 <= '0';
	else 
		Y0 <= '0';
		Y1 <= I;
	end if;
end process;


END TypeArchitecture;

// VHDL entity divizor_frecventa, as the project stores it:
--------------------------------------------------------------------------------
-- Project :
-- File    :
-- Autor   :
-- Date    :
--
--------------------------------------------------------------------------------
-- Description :
--
--------------------------------------------------------------------------------

LIBRARY ieee;
USE ieee.std_logic_1164.all;
USE ieee.std_logic_unsigned.all;


ENTITY divizor_frecventa IS
  PORT (
clk_100mhz: in std_logic;
  	reset: in std_logic;
  	clk_1hz: out std_logic
  		);
 
END divizor_frecventa;

--------------------------------------------------------------------------------
--Complete your VHDL description below
--------------------------------------------------------------------------------

ARCHITECTURE TypeArchitecture OF divizor_frecventa IS

BEGIN
	PROCESS(CLK_100mhz)
	variable nr:std_logic_vector(25 downto 0) := (others => '0');
	begin 
		if reset = '1' then
			nr:= (others => '0');
		else
			if clk_100mhz'event and clk_100mhz = '1' then 
				nr := nr +1;
			end if;
		end if;
		clk_1hz <= nr(25);

	end process;


END TypeArchitecture;

// VHDL entity bcd_to_7seg, as the project stores it:
library ieee;
use ieee.std_logic_1164.all;

entity bcd_to_7seg is
  port (
    BCD : in std_logic_vector(3 downto 0);
    seg : out std_logic_vector(6 downto 0)
  );
end entity bcd_to_7seg;

architecture behavioral of bcd_to_7seg is

begin

    seg <= "1111110" when BCD = x"0" else
    		 "0110000" when BCD = x"1" else
    		 "1101101" when BCD = x"2" else
    		 "1111001" when BCD = x"3" else
    		 "0110011" when BCD = x"4" else
    		 "1011011" when BCD = x"5" else
    		 "1011111" when BCD = x"6" else
    		 "1110000" when BCD = x"7" else
    		 "1111111" when BCD = x"8" else
    		 "1111011" when BCD = x"9" else
    		 "0000000";
    		 
end architecture behavioral;

// VHDL entity distribuitor_bani, as the project stores it:
LIBRARY ieee;
USE ieee.std_logic_1164.ALL;
USE ieee.numeric_std.ALL;

ENTITY distribuitor_bani IS
    PORT (
        clk, enb : IN STD_LOGIC;
        suma : IN STD_LOGIC_VECTOR(15 DOWNTO 0);

        cashreg10, cashreg20, cashreg50, cashreg100, cashreg200, cashreg500 : IN STD_LOGIC_VECTOR(3 DOWNTO 0); 
        bani10, bani20, bani50, bani100, bani200, bani500: OUT STD_LOGIC_VECTOR(3 DOWNTO 0);
        rest10, rest20, rest50, rest100, rest200, rest500 : OUT STD_LOGIC_VECTOR(3 DOWNTO 0);
        
	   eroare : OUT STD_LOGIC;
        done : OUT STD_LOGIC
    );
END ENTITY distribuitor_bani;

ARCHITECTURE Behavioral OF distribuitor_bani IS
    TYPE stare_type IS (idle, procesare_10, procesare_20, procesare_50, procesare_100, procesare_200, procesare_500);
    SIGNAL stare : stare_type := idle;
BEGIN
    PROCESS (clk)
        VARIABLE sum_integer : INTEGER;
        VARIABLE b10, b20, b50, b100, b200, b500 : INTEGER; -- numarul de bancnote disponibile
    BEGIN
        IF rising_edge(clk) THEN
            CASE stare IS
                WHEN idle =>
                    IF enb = '1' THEN
                        sum_integer := to_integer(unsigned(suma));
                        b10 := to_integer(unsigned(cashreg10));
                        b20 := to_integer(unsigned(cashreg20));
                        b50 := to_integer(unsigned(cashreg50));
                        b100 := to_integer(unsigned(cashreg100));
                        b200 := to_integer(unsigned(cashreg200));
                        b500 := to_integer(unsigned(cashreg500));

                        done <= '0';
                        eroare <= '0';
                        stare <= procesare_500;

					if sum_integer > 1000 then 
						eroare <= '1';
                        		stare <= idle;
                        	end if;
                        
                    END IF;

                WHEN procesare_500 =>
                    IF sum_integer >= 500 AND b500 > 0 THEN
                        b500 := b500 - 1;
                        sum_integer := sum_integer - 500;
                    ELSE
                        stare <= procesare_200;
                    END IF;

                WHEN procesare_200 =>
                    IF sum_integer >= 200 AND b200 > 0 THEN
                        b200 := b200 - 1;
                        sum_integer := sum_integer - 200;
                    ELSE
                        stare <= procesare_100;
                    END IF;

                WHEN procesare_100 =>
                    IF sum_integer >= 100 AND b100 > 0 THEN
                        b100 := b100 - 1;
                        sum_integer := sum_integer - 100;
                    ELSE
                        stare <= procesare_50;
                    END IF;

                WHEN procesare_50 =>
                    IF sum_integer >= 50 AND b50 > 0 THEN
                        b50 := b50 - 1;
                        sum_integer := sum_integer - 50;
                    ELSE
                        stare <= procesare_20;
                    END IF;
                    
                WHEN procesare_20 =>
                    IF sum_integer >= 20 AND b20 > 0 THEN
                        b20 := b20 - 1;
                        sum_integer := sum_integer - 20;
                    ELSE
                        stare <= procesare_10;
                    END IF;

                WHEN procesare_10 =>
                    IF sum_integer >= 10 AND b10 > 0 THEN
                        b10 := b10 - 1;
                        sum_integer := sum_integer - 10;
                    ELSE
                        IF sum_integer > 0 THEN
                            eroare <= '1';
                        ELSE
                            rest500 <= STD_LOGIC_VECTOR(to_unsigned(b500, 4));
                            rest200 <= STD_LOGIC_VECTOR(to_unsigned(b200, 4));
                            rest100 <= STD_LOGIC_VECTOR(to_unsigned(b100, 4));
                            rest50 <= STD_LOGIC_VECTOR(to_unsigned(b50, 4));
                            rest20 <= STD_LOGIC_VECTOR(to_unsigned(b20, 4));
                            rest10 <= STD_LOGIC_VECTOR(to_unsigned(b10, 4));

                            bani500 <= STD_LOGIC_VECTOR(to_unsigned(to_integer(unsigned(cashreg500)) - b500, 4));
                            bani200 <= STD_LOGIC_VECTOR(to_unsigned(to_integer(unsigned(cashreg200)) - b200, 4));
                            bani100 <= STD_LOGIC_VECTOR(to_unsigned(to_integer(unsigned(cashreg100)) - b100, 4));
                            bani50 <= STD_LOGIC_VECTOR(to_unsigned(to_integer(unsigned(cashreg50)) - b50, 4));
                            bani20 <= STD_LOGIC_VECTOR(to_unsigned(to_integer(unsigned(cashreg20)) - b20, 4));
                            bani10 <= STD_LOGIC_VECTOR(to_unsigned(to_integer(unsigned(cashreg10)) - b10, 4));

                            done <= '1';
                            eroare <= '0';
                        END IF;
                        stare <= idle;
                    END IF;

            END CASE;
        END IF;
    END PROCESS;
END ARCHITECTURE Behavioral;

// VHDL entity cash_register, as the project stores it:
--------------------------------------------------------------------------------
-- Project :
-- File    :
-- Autor   :
-- Date    :
--
--------------------------------------------------------------------------------
-- Description :
--
--------------------------------------------------------------------------------

LIBRARY ieee;
USE ieee.std_logic_1164.all;

ENTITY cash_register IS
  PORT (clk: in std_logic;
  we: in std_logic;
  rest10, rest20, rest50, rest100, rest200, rest500: in std_logic_vector(3 downto 0);
  cashreg10, cashreg20, cashreg50, cashreg100, cashreg200, cashreg500: out std_logic_vector(3 downto 0)
  );
END cash_register;

--------------------------------------------------------------------------------
--Complete your VHDL description below
--------------------------------------------------------------------------------

ARCHITECTURE TypeArchitecture OF cash_register IS

BEGIN
	process(clk)
	variable b10: std_logic_vector(3 downto 0):="1111";
	variable b20: std_logic_vector(3 downto 0):="1111";
	variable b50: std_logic_vector(3 downto 0):="1111";
	variable b100: std_logic_vector(3 downto 0):="1111";
	variable b200: std_logic_vector(3 downto 0):="1111";
	variable b500: std_logic_vector(3 downto 0):="1111";
	begin
		if rising_edge(clk) then
			if we = '0' then
				b10 := b10;
				b20 := b20;
				b50 := b50;
				b100 := b100;
				b200 := b200;
				b500 := b500;
			else b10 := rest10;
				b20 := rest20;
				b50 := rest50;
				b100 := rest100;
				b200 := rest200;
				b500 := rest500;
			end if;
		end if;
	cashreg10 <= b10;
	cashreg20 <= b20;
	cashreg50 <= b50;
	cashreg100 <= b100;
	cashreg200 <= b200;
	cashreg500 <= b500;
	end process;
END TypeArchitecture;

// VHDL entity binary_to_bcd, as the project stores it:
--------------------------------------------------------------------------------
-- Project :
-- File    :
-- Autor   :
-- Date    :
--
--------------------------------------------------------------------------------
-- Description :
--
--------------------------------------------------------------------------------

LIBRARY ieee;
USE ieee.std_logic_1164.all;
USE ieee.numeric_std.ALL;

ENTITY binary_to_bcd IS
  PORT (bin: in std_logic_vector(15 downto 0);
  bcd0: out std_logic_vector(3 downto 0);
  bcd1: out std_logic_vector(3 downto 0);
  bcd2: out std_logic_vector(3 downto 0);
  bcd3: out std_logic_vector(3 downto 0);
  bcd4: out std_logic_vector(3 downto 0)
  );
END binary_to_bcd;

--------------------------------------------------------------------------------
--Complete your VHDL description below
--------------------------------------------------------------------------------

ARCHITECTURE TypeArchitecture OF binary_to_bcd IS

BEGIN
	process(bin)
	variable tmp, rest: integer;
	begin
	tmp:=to_integer(unsigned(bin));
	rest:=tmp mod 10;
	bcd0<=std_logic_vector(to_unsigned(rest, 4));
	
	tmp:=tmp / 10;
	rest:=tmp mod 10;
	bcd1<=std_logic_vector(to_unsigned(rest, 4));
	
	tmp:=tmp / 10;
	rest:=tmp mod 10;
	bcd2<=std_logic_vector(to_unsigned(rest, 4));
	
	tmp:=tmp / 10;
	rest:=tmp mod 10;
	bcd3<=std_logic_vector(to_unsigned(rest, 4));

	tmp:=tmp / 10;
	rest:=tmp mod 10;
	bcd4<=std_logic_vector(to_unsigned(rest, 4));
	end process;
END TypeArchitecture;

// VHDL entity registru_16_incarcare1, as the project stores it:
--------------------------------------------------------------------------------
-- Project :
-- File    :
-- Autor   :
-- Date    :
--
--------------------------------------------------------------------------------
-- Description :
--
--------------------------------------------------------------------------------

LIBRARY ieee;
USE ieee.std_logic_1164.all;

ENTITY registru_16_incarcare1 IS
  PORT (
  		clk: in std_logic;
  		we: in std_logic;
  		incarcare: in std_logic_vector (15 downto 0);	
 		iesire: out std_logic_vector ( 15 downto 0)
    );
END registru_16_incarcare1;

--------------------------------------------------------------------------------
--Complete your VHDL description below
--------------------------------------------------------------------------------

ARCHITECTURE TypeArchitecture OF registru_16_incarcare1 IS

BEGIN
	process (clk)
	variable reg: std_logic_vector(15 downto 0):=x"1194"; --4500
	begin
		if clk'event and clk = '1' then 
			if we = '1' then
				reg := incarcare;
			else reg:=reg;
			end if;
		end if;
		iesire<= reg;
	end process;

END TypeArchitecture;


--nu merge initializat incarcare in entitate

// VHDL entity registru_16_incarcare2, as the project stores it:
--------------------------------------------------------------------------------
-- Project :
-- File    :
-- Autor   :
-- Date    :
--
--------------------------------------------------------------------------------
-- Description :
--
--------------------------------------------------------------------------------

LIBRARY ieee;
USE ieee.std_logic_1164.all;

ENTITY registru_16_incarcare2 IS
  PORT (
  		clk: in std_logic;
  		we: in std_logic;
  		incarcare: in std_logic_vector (15 downto 0);	
 		iesire: out std_logic_vector ( 15 downto 0)
    );
END registru_16_incarcare2;

--------------------------------------------------------------------------------
--Complete your VHDL description below
--------------------------------------------------------------------------------

ARCHITECTURE TypeArchitecture OF registru_16_incarcare2 IS

BEGIN
	process (clk)
	variable reg: std_logic_vector(15 downto 0):=x"02C6"; --710
	begin
		if clk'event and clk = '1' then 
			if we = '1' then
				reg := incarcare;
			else reg:=reg;
			end if;
		end if;
		iesire<= reg;
	end process;

END TypeArchitecture;


--nu merge initializat incarcare in entitate

// VHDL entity registru_16_incarcare3, as the project stores it:
--------------------------------------------------------------------------------
-- Project :
-- File    :
-- Autor   :
-- Date    :
--
--------------------------------------------------------------------------------
-- Description :
--
--------------------------------------------------------------------------------

LIBRARY ieee;
USE ieee.std_logic_1164.all;

ENTITY registru_16_incarcare3 IS
  PORT (
  		clk: in std_logic;
  		we: in std_logic;
  		incarcare: in std_logic_vector (15 downto 0);	
 		iesire: out std_logic_vector ( 15 downto 0)
    );
END registru_16_incarcare3;

--------------------------------------------------------------------------------
--Complete your VHDL description below
--------------------------------------------------------------------------------

ARCHITECTURE TypeArchitecture OF registru_16_incarcare3 IS

BEGIN
	process (clk)
	variable reg: std_logic_vector(15 downto 0):=x"0CA8"; --3240
	begin
		if clk'event and clk = '1' then 
			if we = '1' then
				reg := incarcare;
			else reg:=reg;
			end if;
		end if;
		iesire<= reg;
	end process;

END TypeArchitecture;


--nu merge initializat incarcare in entitate

// VHDL entity mux_ssd, as the project stores it:
--------------------------------------------------------------------------------
-- Project :
-- File    :
-- Autor   :
-- Date    :
--
--------------------------------------------------------------------------------
-- Description :
--
--------------------------------------------------------------------------------

LIBRARY ieee;
USE ieee.std_logic_1164.all;

ENTITY mux_ssd IS
  PORT (i0, i1, i2: in std_logic_vector(3 downto 0);
  sel: in std_logic_vector(1 downto 0);
  y: out std_logic_vector(3 downto 0));
END mux_ssd;

--------------------------------------------------------------------------------
--Complete your VHDL description below
--------------------------------------------------------------------------------

ARCHITECTURE TypeArchitecture OF mux_ssd IS

BEGIN
	process(i0 ,i1 ,i2 , sel)
	begin
	case sel is
		when "00" => y <= i0;
		when "01" => y <= i1;
		when "10" => y <= i2;
		when others => y <="0000";
	end case;
	end process;

END TypeArchitecture;

// VHDL entity comparator_sold_suma, as the project stores it:
--------------------------------------------------------------------------------
-- Project :
-- File    :
-- Autor   :
-- Date    :
--
--------------------------------------------------------------------------------
-- Description :
--
--------------------------------------------------------------------------------

LIBRARY ieee;
USE ieee.std_logic_1164.all;

ENTITY comparator_sold_suma IS
  PORT (
  data1: in std_logic_vector(15 downto 0);
  data2: in std_logic_vector(15 downto 0);
  i: out std_logic)
;
END comparator_sold_suma;

--------------------------------------------------------------------------------
--Complete your VHDL description below
--------------------------------------------------------------------------------

ARCHITECTURE TypeArchitecture OF comparator_sold_suma IS

BEGIN
	process(data1, data2)
		begin
			if data1 <= data2 then
				i <= '0';
			else i <= '1';
			end if;
	end process;
END TypeArchitecture;

// VHDL entity optiuni_retragere_suma, as the project stores it:
--------------------------------------------------------------------------------
-- Project :
-- File    :
-- Autor   :
-- Date    :
--
--------------------------------------------------------------------------------
-- Description :
--
--------------------------------------------------------------------------------

LIBRARY ieee;
USE ieee.std_logic_1164.all;

ENTITY optiuni_retragere_suma IS
  PORT (ret500, ret200, ret100, ret50, ret20, ret10, rets: in std_logic;
  alta_suma: in std_logic_vector(15 downto 0);
  suma: out std_logic_vector(15 downto 0));
END optiuni_retragere_suma;

--------------------------------------------------------------------------------
--Complete your VHDL description below
--------------------------------------------------------------------------------

ARCHITECTURE TypeArchitecture OF optiuni_retragere_suma IS

BEGIN
process(ret500, ret200, ret100, ret50, ret20, ret10, rets, alta_suma)
begin
if ret500 = '1' and ret200 = '0' and ret100 = '0' and ret50 = '0' and ret20 = '0' and ret10 = '0' and rets = '0' then 
suma<=x"01f4";
elsif ret500 = '0' and ret200 = '1' and ret100 = '0' and ret50 = '0' and ret20 = '0' and ret10 = '0' and rets = '0' then 
suma<=x"00c8";
elsif ret500 = '0' and ret200 = '0' and ret100 = '1' and ret50 = '0' and ret20 = '0' and ret10 = '0' and rets = '0' then 
suma<=x"0064";
elsif ret500 = '0' and ret200 = '0' and ret100 = '0' and ret50 = '1' and ret20 = '0' and ret10 = '0' and rets = '0' then 
suma<=x"0032";
elsif ret500 = '0' and ret200 = '0' and ret100 = '0' and ret50 = '0' and ret20 = '1' and ret10 = '0' and rets = '0' then 
suma<=x"0014";
elsif ret500 = '0' and ret200 = '0' and ret100 = '0' and ret50 = '0' and ret20 = '0' and ret10 = '1' and rets = '0' then 
suma<=x"000a";
elsif ret500 = '0' and ret200 = '0' and ret100 = '0' and ret50 = '0' and ret20 = '0' and ret10 = '0' and rets = '1' then 
suma<=alta_suma;
else
suma<=x"0000";
end if;
end process;
END TypeArchitecture;

// VHDL entity bcd_to_binary, as the project stores it:
--------------------------------------------------------------------------------
-- Project :
-- File    :
-- Autor   :
-- Date    :
--
--------------------------------------------------------------------------------
-- Description :
--
--------------------------------------------------------------------------------

LIBRARY ieee;
USE ieee.std_logic_1164.all;
USE ieee.std_logic_unsigned.all;

ENTITY bcd_to_binary IS
  PORT (i0, i1, i2, i3: in std_logic_vector(3 downto 0);
  bin: out std_logic_vector(15 downto 0));
END bcd_to_binary;

--------------------------------------------------------------------------------
--Complete your VHDL description below
--------------------------------------------------------------------------------

ARCHITECTURE TypeArchitecture OF bcd_to_binary IS

BEGIN
	process(i0, i1, i2, i3)
	variable tmp: std_logic_vector(13 downto 0):="00000000000000";
	variable omie:std_logic_vector(9 downto 0):="1111101000";
	variable osuta:std_logic_vector(6 downto 0):="1100100";
	variable zece:std_logic_vector(3 downto 0):="1010";
	begin
	tmp:=i3*omie + i2*osuta + i1*zece + i0;
	bin<="00" & tmp;
	end process;

END TypeArchitecture;

// VHDL entity cash_register_sold, as the project stores it:
--------------------------------------------------------------------------------
-- Project :
-- File    :
-- Autor   :
-- Date    :
--
--------------------------------------------------------------------------------
-- Description :
--
--------------------------------------------------------------------------------

LIBRARY ieee;
USE ieee.std_logic_1164.all;
USE ieee.std_logic_unsigned.all;

ENTITY cash_register_sold IS
  PORT (i10, i20, i50, i100, i200, i500:  in std_logic_vector(3 downto 0);
  sold: out std_logic_vector(15 downto 0));
END cash_register_sold;

--------------------------------------------------------------------------------
--Complete your VHDL description below
--------------------------------------------------------------------------------

ARCHITECTURE TypeArchitecture OF cash_register_sold IS

BEGIN
	process(i10, i20, i50, i100, i200, i500)
	variable tmp: std_logic_vector (13 downto 0):="00000000000000";
	variable aux10, aux20, aux50, aux100, aux200, aux500 : std_logic_vector (13 downto 0);
	begin
	aux10(7 downto 0) := i10*"1010"; aux10(13 downto 8) := "000000";
	aux20(8 downto 0) := i20*"10100"; aux20(13 downto 9) := "00000";
	aux50(9 downto 0) := i50*"110010"; aux50(13 downto 10) := "0000";
	aux100(10 downto 0) := i100*"1100100"; aux100(13 downto 11) := "000";
	aux200(11 downto 0) := i200*"11001000"; aux200(13 downto 12) := "00";
	aux500(12 downto 0) := i500*"111110100"; aux500(13) := '0';
	
	tmp:= aux10 + aux20 + aux50 + aux100 + aux200 + aux500;
	sold<="00" & tmp;
	end process;

END TypeArchitecture;

// VHDL entity mux_ssd4, as the project stores it:
--------------------------------------------------------------------------------
-- Project :
-- File    :
-- Autor   :
-- Date    :
--
--------------------------------------------------------------------------------
-- Description :
--
--------------------------------------------------------------------------------

LIBRARY ieee;
USE ieee.std_logic_1164.all;

ENTITY mux_ssd4 IS
  PORT (
  i0, i2: in std_logic_vector(3 downto 0);
  sel: in std_logic_vector(1 downto 0);
  y: out std_logic_vector(3 downto 0));
END mux_ssd4;

--------------------------------------------------------------------------------
--Complete your VHDL description below
--------------------------------------------------------------------------------

ARCHITECTURE TypeArchitecture OF mux_ssd4 IS

BEGIN

	process(i0 ,i2 , sel)
	begin
	case sel is
		when "00" => y <= i0;
		when "01" => y <= "0000";
		when "10" => y <= i2;
		when others => y <="0000";
	end case;
	end process;

END TypeArchitecture;

// VHDL entity mux_in_or0_4bit, as the project stores it:
--------------------------------------------------------------------------------
-- Project :
-- File    :
-- Autor   :
-- Date    :
--
--------------------------------------------------------------------------------
-- Description :
--
--------------------------------------------------------------------------------

LIBRARY ieee;
USE ieee.std_logic_1164.all;

ENTITY mux_in_or0_4bit IS
  PORT (
  		I: in std_logic_vector (3 downto 0);
  		S: in std_logic;
  		Y: out std_logic_vector (3 downto 0)
    );
END mux_in_or0_4bit;

--------------------------------------------------------------------------------
--Complete your VHDL description below
--------------------------------------------------------------------------------

ARCHITECTURE TypeArchitecture OF mux_in_or0_4bit IS

BEGIN
process (S, I)	--se va schimba iesirea la modificarea intrarilor
	begin
	if S = '0'THEN Y <= "0000";
	else Y <= I;
	end if;
end process;


END TypeArchitecture;

// VHDL entity bills_to_sum, as the project stores it:
--------------------------------------------------------------------------------
-- Project :
-- File    :
-- Autor   :
-- Date    :
--
--------------------------------------------------------------------------------
-- Description :
--
--------------------------------------------------------------------------------

LIBRARY ieee;
USE ieee.std_logic_1164.all;
USE ieee.numeric_std.ALL;

ENTITY bills_to_sum IS
  PORT (
		  bani10, bani20, bani50, bani100, bani200, bani500: in STD_LOGIC_VECTOR(3 DOWNTO 0);
		  sum: out std_logic_vector(15 downto 0)
    );
END bills_to_sum;

--------------------------------------------------------------------------------
--Complete your VHDL description below
--------------------------------------------------------------------------------

ARCHITECTURE TypeArchitecture OF bills_to_sum IS

BEGIN

process (bani10, bani20, bani50, bani100, bani200, bani500)
variable aux :integer;
variable b10, b20, b50, b100, b200, b500: integer;
begin
b10:= to_integer(unsigned(bani10));
b20:= to_integer(unsigned(bani20));
b50:= to_integer(unsigned(bani50));
b100:= to_integer(unsigned(bani100));
b200:= to_integer(unsigned(bani200));
b500:= to_integer(unsigned(bani500));

aux:= 10*b10 + 20*b20 + 50*b50 + 100*b100 + 200*b200 + 500*b500;

sum <= STD_LOGIC_VECTOR(to_unsigned(aux, 16));

end process;

END TypeArchitecture;

// VHDL entity mux_3in16bit, as the project stores it:
--------------------------------------------------------------------------------
-- Project :
-- File    :
-- Autor   :
-- Date    :
--
--------------------------------------------------------------------------------
-- Description :
--
--------------------------------------------------------------------------------

LIBRARY ieee;
USE ieee.std_logic_1164.all;

ENTITY mux_3in16bit IS
  PORT (
  		I0, I1, I2: in std_logic_vector (15 downto 0);
  		S: in std_logic_vector (1 downto 0);
  		Y: out std_logic_vector (15 downto 0)
    );
END mux_3in16bit;

--------------------------------------------------------------------------------
--Complete your VHDL description below
--------------------------------------------------------------------------------

ARCHITECTURE TypeArchitecture OF mux_3in16bit IS

BEGIN
process (S, I0, I1, I2)	--se va schimba iesirea la modificarea intrarilor
	begin
	if S = "00" THEN Y <= I0;
	elsif S = "01"THEN Y <= I1;
	elsif S = "10"THEN Y <= I2;
	else Y <= x"0000";
	end if;

end process;


END TypeArchitecture;

// VHDL entity demux_4out1bit, as the project stores it:
--------------------------------------------------------------------------------
-- Project :
-- File    :
-- Autor   :
-- Date    :
--
--------------------------------------------------------------------------------
-- Description :
--
--------------------------------------------------------------------------------

LIBRARY ieee;
USE ieee.std_logic_1164.all;

ENTITY demux_4out1bit IS
  PORT (
  		I: in std_logiC;
  		S: in std_logic_vector (1 downto 0);
  		Y0, Y1, Y2, Y3: out std_logic
    );
END demux_4out1bit;

--------------------------------------------------------------------------------
--Complete your VHDL description below
--------------------------------------------------------------------------------

ARCHITECTURE TypeArchitecture OF demux_4out1bit IS

BEGIN
process (S, I)
	begin
	if S = "00"THEN 
		Y0 <= I;
		Y1 <= '0';
		Y2 <= '0';
		Y3 <= '0';
	elsif S = "01" then
		Y0 <= '0';
		Y1 <= I;
		Y2 <= '0';
		Y3 <= '0';
	elsif S = "10" then 
		Y0 <= '0';
		Y1 <= '0';
		Y2 <= I;
		Y3 <= '0';
	else
		Y0 <= '0';
		Y1 <= '0';
		Y2 <= '0';
		Y3 <= I;
	end if;
end process;


END TypeArchitecture;

// VHDL entity sum_nr_bills, as the project stores it:
--------------------------------------------------------------------------------
-- Project :
-- File    :
-- Autor   :
-- Date    :
--
--------------------------------------------------------------------------------
-- Description :
--
--------------------------------------------------------------------------------

LIBRARY ieee;
USE ieee.std_logic_1164.all;
USE ieee.std_logic_unsigned.all;


ENTITY sum_nr_bills IS
  PORT (
  	cashreg10, cashreg20, cashreg50, cashreg100, cashreg200, cashreg500 : IN STD_LOGIC_VECTOR(3 DOWNTO 0); 
  	bani10, bani20, bani50, bani100, bani200, bani500: in STD_LOGIC_VECTOR(3 DOWNTO 0);
  	newreg10, newreg20, newreg50, newreg100, newreg200, newreg500 : out STD_LOGIC_VECTOR(3 DOWNTO 0)
  	
    );
END sum_nr_bills;

--------------------------------------------------------------------------------
--Complete your VHDL description below
--------------------------------------------------------------------------------

ARCHITECTURE TypeArchitecture OF sum_nr_bills IS

BEGIN

process (cashreg10, cashreg20, cashreg50, cashreg100, cashreg200, cashreg500, bani10, bani20, bani50, bani100, bani200, bani500)
variable A10, A20, A50, A100, A200, A500, B10, B20, B50, B100, B200, B500, aux10, aux20, aux50, aux100, aux200, aux500: std_logic_vector(4 downto 0) := "00000";
begin
A10 (3 DOWNTO 0) := cashreg10;
A10(4) := '0';
A20 (3 DOWNTO 0) := cashreg20;
A20(4) := '0';
A50 (3 DOWNTO 0) := cashreg50;
A50(4) := '0';
A100 (3 DOWNTO 0) := cashreg100;
A100(4) := '0';
A200 (3 DOWNTO 0) := cashreg200;
A200(4) := '0';
A500 (3 DOWNTO 0) := cashreg500;
A500(4) := '0';

B10 (3 DOWNTO 0) := bani10;
B10(4) := '0';
B20 (3 DOWNTO 0) := bani20;
B20(4) := '0';
B50 (3 DOWNTO 0) := bani50;
B50(4) := '0';
B100 (3 DOWNTO 0) := bani100;
B100(4) := '0';
B200 (3 DOWNTO 0) := bani200;
B200(4) := '0';
B500 (3 DOWNTO 0) := bani500;
B500(4) := '0';


aux10 := A10+B10;
aux20 := A20+B20;
aux50 := A50+B50;
aux100 := A100+B100;
aux200 := A200+B200;
aux500 := A500+B500;

if aux10(4) = '1' then aux10(3 downto 0) := "1111";
end if;
if aux20(4) = '1' then aux20(3 downto 0) := "1111";
end if;
if aux50(4) = '1' then aux50(3 downto 0) := "1111";
end if;
if aux100(4) = '1' then aux100(3 downto 0) := "1111";
end if;
if aux200(4) = '1' then aux200(3 downto 0) := "1111";
end if;
if aux500(4) = '1' then aux500(3 downto 0) := "1111";
end if;


newreg10 <= aux10(3 downto 0);
newreg20 <= aux20(3 downto 0);
newreg50 <= aux50(3 downto 0);
newreg100 <= aux100(3 downto 0);
newreg200 <= aux200(3 downto 0);
newreg500 <= aux500(3 downto 0);



end process;


END TypeArchitecture;

// VHDL entity mux_for_cash_reg, as the project stores it:
--------------------------------------------------------------------------------
-- Project :
-- File    :
-- Autor   :
-- Date    :
--
--------------------------------------------------------------------------------
-- Description :
--
--------------------------------------------------------------------------------

LIBRARY ieee;
USE ieee.std_logic_1164.all;

ENTITY mux_for_cash_reg IS
  PORT (
  		alg10, alg20, alg50, alg100, alg200, alg500, dep10, dep20, dep50, dep100, dep200, dep500: in std_logic_vector (3 downto 0);
  		sel: in std_logic;
  		reg10, reg20, reg50, reg100, reg200, reg500: out std_logic_vector (3 downto 0)
    );
END mux_for_cash_reg;

--------------------------------------------------------------------------------
--Complete your VHDL description below
--------------------------------------------------------------------------------

ARCHITECTURE TypeArchitecture OF mux_for_cash_reg IS

BEGIN

process (alg10, alg20, alg50, alg100, alg200, alg500, dep10, dep20, dep50, dep100, dep200, dep500, sel)
begin

if sel = '0' then
		reg10 <= alg10;
		reg20 <= alg20;
		reg50 <= alg50;
		reg100 <= alg100;
		reg200 <= alg200;
		reg500 <= alg500;
else 
		reg10 <= dep10;
		reg20 <= dep20;
		reg50 <= dep50;
		reg100 <= dep100;
		reg200 <= dep200;
		reg500 <= dep500;
end if;


end process;



END TypeArchitecture;
